# Fritzing sketch proyectofin (saved by Fritzing 1.0.5)

parts:
  J1 = Camdenboss CTB0158-8 [part_number=CTB0158-8 package=THT]
  LED_1_PRINCIPAL = smd LED [color="Red (633nm)" package="0603 [SMD]"]
  LED_2_PANEL = smd LED [color="Red (633nm)" package="0603 [SMD]"]
  ventilador_(simulado) = DC Motor [voltage_(max)=6V voltage_(min)=3V]
  R1 = Resistor [tolerance=±5% resistance=220 package="2010 [SMD]"]
  VR1 = LM2596 (TO263) [part_number=LM2596 package=TO263]
  JACK1 = 2.1mm DC Barrel Jack
  R2 = Resistor [tolerance=±5% power=0.25W resistance=220 package=THT]
  Componente1 = Arduino Ethernet Shield (Rev3)
  U1 = Module 4 Relais 5V [package="Module 4 Relais 5V"]
  J2 = Buzzer

nets:
  N1: J1.pin1, Componente1.GND, J2.pin1
  N2: J1.pin2, VR1.Pin_3, VR1.Tab, JACK1.sleeve
  N3: J1.pin4, U1.GND
  N4: J1.pin5, LED_1_PRINCIPAL.cathode
  N5: J1.pin6, ventilador_(simulado).pin_2
  N6: J1.pin7, LED_2_PANEL.cathode
  N7: LED_1_PRINCIPAL.anode, R2.Pin_1
  N8: LED_2_PANEL.anode, R1.Pin_1
  N9: R1.Pin_0, U1.K3-NO
  N10: VR1.Pin_1, JACK1.center, U1.K2-Com
  N11: VR1.Pin_2, U1.K1-Com, U1.K3-Com
  N12: R2.Pin_0, U1.K1-NO
  5V: Componente1.5V, U1.VCC
  N13: Componente1.D8, U1.IN2
  N14: Componente1.PWM_D9, J2.pin2
  N15: Componente1.SPI/D12, U1.IN3
  N16: Componente1.SPI/D13, U1.IN4
  N17: Componente1.D7, U1.IN1

custom parts:
  2.1mm DC Barrel Jack: 2.1mm DC Barrel Jack with Thru-Hole Connectors (breadboardable)
  Module 4 Relais 5V: Module 4 Relais 5V 4x SPD-06VDC-SD-C
  Buzzer: Fixed frequency buzzer
